// Logisim project 4-bit multiplier.circ as structural Verilog: 1 circuit, main circuit main
module main (
  input  A3,
  input  A2,
  input  A1,
  input  A0,
  input  B3,
  input  B2,
  input  B1,
  input  B0,
  output P5,
  output P4,
  output P3,
  output P2,
  output P1,
  output P0
);

  wire A0B1_out, A0B2_out, A1B0_out, A1B1_out, A1B2_out, A2B0_out, A2B1_out, A2B2_out, A3B0_out, nand_1_out,
       nand_2_out, nand_3_out, nand_4_out, nand_5_out, nand_6_out, nand_7_out, nand_8_out, nand_11_out,
       nand_12_out, nand_13_out, nand_14_out, nand_15_out, nand_16_out, nand_17_out, nand_18_out,
       nand_19_out, nand_20_out, nand_21_out, nand_22_out, nand_23_out, nand_24_out, nand_25_out,
       nand_27_out, nand_28_out, nand_29_out, nand_30_out, nand_31_out, nand_32_out, nand_33_out,
       nand_34_out, nand_35_out, nand_36_out, nand_37_out, nand_38_out, nand_40_out, nand_41_out,
       nand_42_out, nand_43_out, nand_44_out, nand_45_out, nand_46_out, nand_47_out, nand_48_out,
       nand_49_out, nand_51_out, nand_52_out;

  nand nand_1 (nand_1_out, B2, A2);
  nand nand_2 (nand_2_out, A2B2_out, nand_22_out);
  nand A2B2 (A2B2_out, nand_1_out, nand_1_out);
  nand nand_3 (nand_3_out, A2B2_out, nand_2_out);
  nand nand_4 (nand_4_out, nand_2_out, nand_22_out);
  nand nand_5 (nand_5_out, nand_3_out, nand_4_out);
  nand nand_6 (nand_6_out, nand_5_out, nand_27_out);
  nand nand_7 (nand_7_out, nand_5_out, nand_6_out);
  nand nand_8 (nand_8_out, nand_6_out, nand_27_out);
  nand nand_9 (P4, nand_7_out, nand_8_out);
  nand nand_10 (P5, nand_6_out, nand_2_out);
  nand nand_11 (nand_11_out, B2, A1);
  nand nand_12 (nand_12_out, B0, A3);
  nand nand_13 (nand_13_out, B1, A2);
  nand nand_14 (nand_14_out, nand_44_out, A2B1_out);
  nand A1B2 (A1B2_out, nand_11_out, nand_11_out);
  nand nand_15 (nand_15_out, nand_21_out, A1B2_out);
  nand A3B0 (A3B0_out, nand_12_out, nand_12_out);
  nand A2B1 (A2B1_out, nand_13_out, nand_13_out);
  nand nand_16 (nand_16_out, nand_44_out, nand_14_out);
  nand nand_17 (nand_17_out, nand_14_out, A2B1_out);
  nand nand_18 (nand_18_out, nand_21_out, nand_15_out);
  nand nand_19 (nand_19_out, nand_15_out, A1B2_out);
  nand nand_20 (nand_20_out, nand_18_out, nand_19_out);
  nand nand_21 (nand_21_out, nand_16_out, nand_17_out);
  nand nand_22 (nand_22_out, nand_14_out, nand_14_out);
  nand nand_23 (nand_23_out, nand_20_out, nand_40_out);
  nand nand_24 (nand_24_out, nand_20_out, nand_23_out);
  nand nand_25 (nand_25_out, nand_23_out, nand_40_out);
  nand nand_26 (P3, nand_24_out, nand_25_out);
  nand nand_27 (nand_27_out, nand_23_out, nand_15_out);
  nand nand_28 (nand_28_out, B1, A1);
  nand nand_29 (nand_29_out, B2, A0);
  nand nand_30 (nand_30_out, B0, A2);
  nand A1B1 (A1B1_out, nand_28_out, nand_28_out);
  nand nand_31 (nand_31_out, A2B0_out, A1B1_out);
  nand A0B2 (A0B2_out, nand_29_out, nand_29_out);
  nand A2B0 (A2B0_out, nand_30_out, nand_30_out);
  nand nand_32 (nand_32_out, A2B0_out, nand_31_out);
  nand nand_33 (nand_33_out, nand_31_out, A1B1_out);
  nand nand_34 (nand_34_out, nand_43_out, A0B2_out);
  nand nand_35 (nand_35_out, nand_32_out, nand_33_out);
  nand nand_36 (nand_36_out, nand_35_out, nand_51_out);
  nand nand_37 (nand_37_out, nand_43_out, nand_34_out);
  nand nand_38 (nand_38_out, nand_34_out, A0B2_out);
  nand nand_39 (P2, nand_37_out, nand_38_out);
  nand nand_40 (nand_40_out, nand_34_out, nand_34_out);
  nand nand_41 (nand_41_out, nand_35_out, nand_36_out);
  nand nand_42 (nand_42_out, nand_36_out, nand_51_out);
  nand nand_43 (nand_43_out, nand_41_out, nand_42_out);
  nand nand_44 (nand_44_out, nand_36_out, nand_31_out);
  nand nand_45 (nand_45_out, B1, A0);
  nand nand_46 (nand_46_out, B0, A1);
  nand A0B1 (A0B1_out, nand_45_out, nand_45_out);
  nand nand_47 (nand_47_out, A1B0_out, A0B1_out);
  nand A1B0 (A1B0_out, nand_46_out, nand_46_out);
  nand nand_48 (nand_48_out, A1B0_out, nand_47_out);
  nand nand_49 (nand_49_out, nand_47_out, A0B1_out);
  nand nand_50 (P1, nand_48_out, nand_49_out);
  nand nand_51 (nand_51_out, nand_47_out, nand_47_out);
  nand nand_52 (nand_52_out, B0, A0);
  nand A0B0 (P0, nand_52_out, nand_52_out);

  // Notes on the sheet:
  //   A
  //   B
  //   C
  //   Full adder
  //   Sum
  //   Carry out
  //   A
  //   B
  //   A
  //   B
  //   C
  //   Half adder
  //   Full adder
  //   Sum
  //   Carry out
  //   Sum
  //   Carry out
  //   A
  //   B
  //   C
  //   A
  //   B
  //   Full adder
  //   Half adder
  //   Sum
  //   Carry out
  //   Sum
  //   Carry out
  //   A
  //   B
  //   Half adder
  //   Sum
  //   Carry out
  //   B0
  //   A0
  //   B1
  //   A1
  //   B2
  //   A2
  //   B3
  //   A3
endmodule
